# Fritzing sketch esp_sparsnas_gateway_MCUv3 (saved by Fritzing 0.9.3b)
circuit board: 8.8cm x 6cm

parts:
  RFM69HCW = Adafruit RFM69HCW Transceiver Radio [part_number="Adafruit #3070 and #3071"]
  Power_plug1 = Power plug
  C1 = Ceramic Capacitor [capacitance=100nF package="100 mil [THT, multilayer]"]
  L1 = Inductor [inductance=100µH current=275mA package="400 mil [THT]"]
  ANT1 = SMA Antenna Connector [package=sma-edge]
  C2 = Electrolytic Capacitor [package="8mm [THT, electrolytic]"]
  NodeMCU_V3 = NodeMCU V3.0

nets:
  N1: RFM69HCW.ANTENNA, ANT1.SIGNAL
  N2: RFM69HCW.VIN, L1.pin_1
  GND: RFM69HCW.GND, Power_plug1.GND, C1.0, ANT1.GND, C2.-, NodeMCU_V3.GND
  N3: RFM69HCW.EN, NodeMCU_V3.D8
  N4: RFM69HCW.DIO0, NodeMCU_V3.D1
  N5: RFM69HCW.SCK, NodeMCU_V3.D5
  N6: RFM69HCW.MISO, NodeMCU_V3.D6
  N7: RFM69HCW.MOSI, NodeMCU_V3.D7
  VCC: Power_plug1.VCC, C1.1, C2.+, NodeMCU_V3.Vin
  N8: L1.pin_0, NodeMCU_V3.3V3

notes:
  EspSparsnasGateway
  USB this way

custom parts:
  Adafruit RFM69HCW Transceiver Radio: Sending data over long distances is like magic, and now you can be a magician with this range of powerful and easy-to-use radio modules. Sure, sometimes you want to talk to a computer (a good time to use WiFi) or perhaps communicate with a Phone (choose Bluetooth Low Energy!) but what if you want to send data very far? Most WiFi, Bluetooth, Zigbee and other wireless chipsets use 2.4GHz, which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
  Electrolytic Capacitor: electrolytic capacitor, 8mm dia
  NodeMCU V3.0: ESP8266 based NodeMCU
