# Fritzing sketch esp_sparsnas_gateway_MCUv3_version2 (saved by Fritzing 0.9.3b)
circuit board: 8.45633cm x 5.95466cm
breadboards: 1

parts:
  Part1 = Adafruit RFM69HCW Transceiver Radio [part_number="Adafruit #3070 and #3071"]
  U1 = NodeMCU V3.0
  J1 = Power Jack [package=power_jack_pth_lock]
  C2 = Ceramic Capacitor [capacitance=100nF package="100 mil [THT, multilayer]"]
  C1 = Tantalum Capacitor [capacitance=0.47mF package="100 mil [THT, tantalum]"]
  L1 = Inductor [inductance=100µH package="400 mil [THT]"]
  J$1 = SMA Antenna Connector [package=sma-edge]
  J$2 = SMA Antenna Connector [package=sma-edge]
  U2 = NodeMCU V1.0

nets:
  N1: Part1.ANTENNA, J$1.SIGNAL
  N2: Part1.VIN, L1.pin_1
  GND: Part1.GND, U1.GND, J1.GND, J1.GNDBREAK, C2.0, C1.-, J$1.GND, J$2.GND, U2.GND
  N3: Part1.DIO0, U1.D1, U2.D1
  N4: Part1.SCK, U1.D5, U2.D5
  N5: Part1.MISO, U1.D6, U2.D6
  N6: Part1.MOSI, U1.D7, U2.D7
  N7: Part1.CS, U1.D8, U2.D8
  N8: U1.D0, U2.D0
  N9: U1.D2, U2.D2
  N10: U1.D3, U2.D3
  N11: U1.D4, U2.D4
  3V3: U1.3V3, L1.pin_0, U2.3V3
  N12: U1.RX, U2.RX
  N13: U1.TX, U2.TX
  VIN: U1.Vin, J1.PWR, C2.1, C1.+, U2.Vin
  N14: U1.RST, U2.RST
  N15: U1.EN, U2.EN
  N16: U1.SK, U2.CLK
  N17: U1.S0, U2.SD0
  N18: U1.SC, U2.CMD
  N19: U1.S1, U2.SD1
  N20: U1.S2, U2.SD2
  N21: U1.S3, U2.SD3
  N22: U1.A0, U2.A0

custom parts:
  Adafruit RFM69HCW Transceiver Radio: Sending data over long distances is like magic, and now you can be a magician with this range of powerful and easy-to-use radio modules. Sure, sometimes you want to talk to a computer (a good time to use WiFi) or perhaps communicate with a Phone (choose Bluetooth Low Energy!) but what if you want to send data very far? Most WiFi, Bluetooth, Zigbee and other wireless chipsets use 2.4GHz, which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
  NodeMCU V3.0: ESP8266 based NodeMCU
  NodeMCU V1.0: ESP8266 based NodeMCU
